# Fritzing sketch 실제 부품 연결 (saved by Fritzing 1.0.8)
breadboards: 1

parts:
  A1 = ESP32-S3 devkit 1
  M1 = GY-86
  GY-NEO6MV1 = GY-NEO6MV2
  A2 = Hi-link HLK-LD2410C

nets:
  GND: A1.Pin_1, A1.Pin_42, M1.GND, GY-NEO6MV1.GND, A2.Pin_2
  +3V3: A1.Pin_2, A1.Pin_21, M1.+3V3, GY-NEO6MV1.Vcc, A2.Pin_1
  N1: A1.Pin_8, M1.SDA
  N2: A1.Pin_9, M1.SCL
  N3: A1.Pin_10, GY-NEO6MV1.Tx
  N4: A1.Pin_11, GY-NEO6MV1.Rx
  N5: A1.Pin_17, A2.Pin_5
  N6: A1.Pin_18, A2.Pin_4

notes:
  imu
  radar
  gnss

custom parts:
  ESP32-S3 devkit 1: ESP32-S3-DevKitC-1 Development Board BT 2.4G Wifi Module for Arduino 8MB PSRAM 16MB FLASH N16R8 42Pin CH340C Type-C ESP32 S3.
  GY-86: GY-86 10DOF MS5611 HMC5883L MPU6050 Module
  GY-NEO6MV2: Description: Module GPS , type GY-NEO6MV2, pour arduino et autres micro-contrôleurs. Caractéristiques De type GY-NEO6MV2 Alimentation 3V-5V Avec Flight Control EEPROM MWC Antenne large céramique, fort signal, 25 x 25 mm Paramètres de configuration sauvegardés en EEPROM Avec batterie de backup de données LED témoin de signal Module miniaturisé 25 x 35 mm Trou de fixation de 3mm Baud rate par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
  Hi-link HLK-LD2410C: LD2410C is a high-sensitivity 24GHz human presence status sensing module.
